// Logisim project bfcpu.circ as structural Verilog: 4 circuits, main circuit main
module main (
);

  wire and_1_out, controller_1_clk, controller_1_fdec, controller_1_we, demultiplexer_1_out0,
       demultiplexer_1_out1, demultiplexer_1_out2, demultiplexer_1_out3, not_1_out, not_2_out;
  wire [1:0] controller_1_seloperand;
  wire [3:0] rom_1_data;
  wire [7:0] BUF_q, BUF_q_2, controlled_buffer_1_out, controlled_buffer_2_out, controller_1_counter;
  wire [15:0] alu_1_x_prime, DP_q, multiplexer_1_out, PC_q;

  Register #(.width(16), .trigger("rising")) PC (
    .D({BUF_q_2, BUF_q}), .Q(PC_q), .clk(demultiplexer_1_out1));  // open: en, clr
  // Probe on demultiplexer_1_out0
  Demultiplexer #(.select(2), .width(1), .tristate("false")) demultiplexer_1 (
    .out0(demultiplexer_1_out0), .out1(demultiplexer_1_out1), .out2(demultiplexer_1_out2),
    .out3(demultiplexer_1_out3), .in(controller_1_we), .sel(controller_1_seloperand));
  ROM #(.addrWidth(16), .dataWidth(4)) rom_1 (.addr(PC_q), .data(rom_1_data));  // open: sel
  // Probe on rom_1_data
  // Probe on controller_1_we
  Controller controller_1 (
    .Opcode(rom_1_data), .Halt(demultiplexer_1_out0), .WE(controller_1_we), .Clk(controller_1_clk),
    .Counter(controller_1_counter), .selOperand(controller_1_seloperand), .fDec(controller_1_fdec));
  Register #(.width(16), .trigger("rising")) DP (
    .D({BUF_q_2, BUF_q}), .Q(DP_q), .clk(demultiplexer_1_out2));  // open: en, clr
  // Probe on controller_1_clk
  // Probe on controller_1_counter
  // Probe on controller_1_seloperand
  and and_1 (and_1_out, demultiplexer_1_out3, controller_1_we);
  not not_1 (not_1_out, and_1_out);
  // Probe on multiplexer_1_out
  Multiplexer #(.select(2), .width(16)) multiplexer_1 (
    .in1(PC_q), .in2(DP_q), .in3({{8{1'b0}}, controlled_buffer_2_out}), .out(multiplexer_1_out),
    .sel(controller_1_seloperand));  // open: in0
  // Probe on controller_1_fdec
  assign controlled_buffer_1_out = and_1_out ? BUF_q : 8'bz;  // Controlled_Buffer controlled_buffer_1
  RAM #(.addrWidth(16), .dataWidth(8), .bus("asynch")) ram_1 (
    .addr(DP_q), .data(controlled_buffer_1_out), .ld(not_1_out));  // open: sel, clr
  assign controlled_buffer_2_out = not_2_out ? controlled_buffer_1_out : 8'bz;  // Controlled_Buffer controlled_buffer_2
  not not_2 (not_2_out, and_1_out);
  // Probe on alu_1_x_prime
  ALU alu_1 (.x(multiplexer_1_out), .m(controller_1_fdec), .x_prime(alu_1_x_prime));
  // Probe on {BUF_q_2, BUF_q}
  Register #(.width(16), .trigger("rising")) BUF (
    .D(alu_1_x_prime), .Q({BUF_q_2, BUF_q}), .clk(controller_1_clk));  // open: en, clr

  // Notes on the sheet:
  //   PROGRAM ROM
  //   CONTROL UNIT
  //   contents of rom_1 (hex, n*v repeats v):
  //   3 2 3 2 a
  //   DATA RAM
endmodule

module ALU (
  input  [15:0] x,
  input  m,
  output [15:0] x_prime
);

  wire adder_1_cout, adder_2_cout, adder_3_cout;

  Adder #(.width(4)) adder_1 (.a(x[3:0]), .b({{3{m}}, 1'b1}), .out(x_prime[3:0]), .cin(1'b0), .cout(adder_1_cout));
  Adder #(.width(4)) adder_2 (.a(x[7:4]), .b({4{m}}), .out(x_prime[7:4]), .cin(adder_1_cout), .cout(adder_2_cout));
  Adder #(.width(4)) adder_3 (.a(x[11:8]), .b({4{m}}), .out(x_prime[11:8]), .cin(adder_2_cout), .cout(adder_3_cout));
  Adder #(.width(4)) adder_4 (.a(x[15:12]), .b({4{m}}), .out(x_prime[15:12]), .cin(adder_3_cout));  // open: cout
endmodule

module xx (
);

  wire and_1_out, clock_1_out, decoder_1_out1, decoder_1_out2, decoder_1_out3, t_ff_1_qn;
  wire [1:0] multiplexer_1_out;

  Clock #(.highDuration(1), .lowDuration(1)) clock_1 (.out(clock_1_out));
  Register #(.width(8), .trigger("rising")) register_1 (.D(8'hcc), .clk(and_1_out));  // open: en, Q, clr
  and and_1 (and_1_out, t_ff_1_qn, decoder_1_out1);
  T_Flip_Flop #(.trigger("rising")) t_ff_1 (.clk(clock_1_out), .T(1'b1), .Qn(t_ff_1_qn));  // open: Q, preset, reset, en
  Multiplexer #(.select(1), .width(2)) multiplexer_1 (
    .in0(2'b10), .in1(2'b11), .out(multiplexer_1_out), .sel(clock_1_out));
  Decoder #(.select(2), .tristate("false")) decoder_1 (
    .out1(decoder_1_out1), .out2(decoder_1_out2), .out3(decoder_1_out3), .sel(multiplexer_1_out));  // open: out0
  Controlled_Buffer #(.width(1)) controlled_buffer_1 ();  // open: in, out, en
endmodule

module Controller (
  input  [3:0] Opcode,
  input  Halt,
  output WE,
  output Clk,
  output [1:0] selOperand,
  output fDec,
  output [7:0] Counter
);

  wire clock_1_out, t_ff_1_qn, xnor_1_out;
  wire [1:0] counter_1_q;
  wire [2:2] multiplexer_1_out;

  T_Flip_Flop #(.trigger("rising")) t_ff_1 (.clk(Halt), .T(1'b1), .Qn(t_ff_1_qn));  // open: Q, preset, reset, en
  Clock #(.highDuration(1), .lowDuration(1)) clock_1 (.out(clock_1_out));
  and and_1 (Clk, clock_1_out, t_ff_1_qn);
  Counter #(.width(2), .max('h3), .ongoal("wrap"), .trigger("rising")) counter_1 (
    .Q(counter_1_q), .clk(Clk));  // open: load, D, count, carry, clr
  not not_1 (WE, counter_1_q[0]);
  xnor xnor_1 (xnor_1_out, counter_1_q[0], counter_1_q[1]);
  Multiplexer #(.select(1), .width(4)) multiplexer_1 (
    .in0(Opcode), .in1(4'b0001), .out({fDec, multiplexer_1_out[2], selOperand}), .sel(xnor_1_out));
  Counter #(.width(8), .max('hff), .ongoal("wrap"), .trigger("rising")) counter_2 (
    .Q(Counter), .clk(Clk));  // open: load, D, count, carry, clr
endmodule
